// Logisim project hw5fsm.circ as structural Verilog: 1 circuit, main circuit main
// Register
module main (
  input  Input,
  input  Clock,
  output Output
);

  wire not_2_out;
  wire [1:0] not_1_out, Register_q;

  not not_1 (not_1_out[0], Input);
  not not_2 (not_2_out, Register_q[1]);
  and and_1 (Output, not_1_out[0], Register_q[0]);
  and and_2 (not_1_out[1], Input, not_2_out);
  Register #(.width(2)) Register (.D(not_1_out), .Q(Register_q), .clk(Clock));  // open: en, clr

  // Notes on the sheet:
  //   DO NOT MOVE GIVEN PINS
endmodule
