// Logisim project ex1.circ as structural Verilog: 5 circuits, main circuit main
module main (
);

  NAND nand_1 ();  // open: A, B, Out
endmodule

module NAND (
  input  A,
  input  B,
  output Out
);

  wire and_1_out;

  not not_1 (Out, and_1_out);
  and and_1 (and_1_out, A, B);
endmodule

module XOR (
  input  A,
  input  B,
  output out_3
);

  wire AND_2_out, AND_out, not_1_out, not_2_out;

  not not_1 (not_1_out, A);
  not not_2 (not_2_out, B);
  and AND (AND_out, B, not_1_out);
  and AND_2 (AND_2_out, A, not_2_out);
  or or_1 (out_3, AND_out, AND_2_out);
endmodule

module _2_1_MUX (
  input  in_1,
  input  in_2,
  input  in_3,
  output out_4
);

  wire AND_2_out, AND_out, not_1_out;

  not not_1 (not_1_out, in_3);
  and AND (AND_out, in_1, not_1_out);
  and AND_2 (AND_2_out, in_2, in_3);
  or or_1 (out_4, AND_out, AND_2_out);
endmodule

module _4_1_MUX (
  input  A,
  input  B,
  input  C,
  input  D,
  input  S0,
  input  S1,
  output out_7
);

  wire n2_1_mux_1_out_4, n2_1_mux_2_out_4;

  _2_1_MUX u_2_1_mux_1 (.in_1(A), .in_2(B), .in_3(S0), .out_4(n2_1_mux_1_out_4));
  _2_1_MUX u_2_1_mux_2 (.in_1(C), .in_2(D), .in_3(S0), .out_4(n2_1_mux_2_out_4));
  _2_1_MUX u_2_1_mux_3 (.in_1(n2_1_mux_1_out_4), .in_2(n2_1_mux_2_out_4), .in_3(S1), .out_4(out_7));
endmodule
