// Logisim project ex1.circ as structural Verilog: 1 circuit, main circuit main
module main (
  input  [7:0] Input,
  output out_2,
  output [7:0] out_3
);

  and and_1 (out_2, Input[0], Input[7]);
  not not_1 (out_3[7], Input[7]);

  assign out_3[6:0] = Input[6:0];
endmodule
