// Logisim project rotr.circ as structural Verilog: 5 circuits, main circuit main
// 1
module main (
  input  [3:0] in_1,
  input  [15:0] in_2,
  output [15:0] out_3
);

  wire [15:0] subcirc1_1_out_3, subcirc2_1_out_3, subcirc4_1_out_3;

  subcirc1 subcirc1_1 (.in_1(in_1[0]), .in_2(in_2), .out_3(subcirc1_1_out_3));
  subcirc4 subcirc4_1 (.in_1(in_1[2]), .in_2(subcirc2_1_out_3), .out_3(subcirc4_1_out_3));
  subcirc2 subcirc2_1 (.in_1(in_1[1]), .in_2(subcirc1_1_out_3), .out_3(subcirc2_1_out_3));
  subcirc8 subcirc8_1 (.in_1(in_1[3]), .in_2(subcirc4_1_out_3), .out_3(out_3));

  // Other names for the same wires on the sheet: _1 = in_1[0]; _2 = in_1[1]; _3 = in_1[2]; _4 = in_1[3]
endmodule

module subcirc1 (
  input  in_1,
  input  [15:0] in_2,
  output [15:0] out_3
);

  Multiplexer #(.width(16), .enable("false")) multiplexer_1 (
    .in0(in_2), .in1({in_2[0], in_2[15:1]}), .out(out_3), .sel(in_1));
endmodule

module subcirc2 (
  input  in_1,
  input  [15:0] in_2,
  output [15:0] out_3
);

  Multiplexer #(.width(16), .enable("false")) multiplexer_1 (
    .in0(in_2), .in1({in_2[1:0], in_2[15:2]}), .out(out_3), .sel(in_1));
endmodule

module subcirc4 (
  input  in_1,
  input  [15:0] in_2,
  output [15:0] out_3
);

  Multiplexer #(.width(16), .enable("false")) multiplexer_1 (
    .in0(in_2), .in1({in_2[3:0], in_2[15:4]}), .out(out_3), .sel(in_1));
endmodule

module subcirc8 (
  input  in_1,
  input  [15:0] in_2,
  output [15:0] out_3
);

  Multiplexer #(.width(16), .enable("false")) multiplexer_1 (
    .in0(in_2), .in1({in_2[7:0], in_2[15:8]}), .out(out_3), .sel(in_1));
endmodule
