// Logisim project alu_backup.circ as structural Verilog: 3 circuits, main circuit main
module main (
  input  [15:0] X,
  input  [15:0] Y,
  input  [3:0] switch__S,
  input  in_4,
  input  in_5,
  output signed_overflow,
  output [15:0] result,
  output equal
);

  wire lowerOverflow2, lowerOverflow3, lowerOverflow4, lowerOverflow5, signedOverflow2, signedOverflow3,
       signedOverflow4, signedOverflow5, signedOverflow9, undriven, undriven_2, undriven_3, undriven_4,
       undriven_5, undriven_6, upperOverflow2, upperOverflow3, upperOverflow4, upperOverflow5;
  wire [7:0] negator_2_out, negator_3_out, negator_4_out, negator_5_out;
  wire [15:0] operation0inX, operation0inY, operation1inX, operation1inY, operation2inX, operation2inY,
       operation3inX, operation3inY, operation4inX, operation4inY, operation5inX, operation5inY,
       operation6inX, operation6inY, operation7inX, operation7inY, operation8inX, operation8inY,
       operation9inX, operation9inY, operation10inX, operation10inY, operation11inX, operation11inY,
       operation12inX, operation12inY, result0, result1, result2, result3, result4, result5, result6,
       result7, result8, result9, result10, result11, result12;

  // Probe on X
  // Probe on Y
  Negator #(.width(1)) negator_1 ();  // open: in, out
  Multiplexer #(.select(4), .enable("false")) multiplexer_1 (
    .in0(in_4), .in1(in_4), .in2(signedOverflow2), .in3(signedOverflow3), .in4(signedOverflow4),
    .in5(signedOverflow5), .in6(in_4), .in7(in_4), .in8(in_4), .in9(signedOverflow9), .in10(undriven),
    .in11(undriven_2), .in12(undriven_3), .out(signed_overflow), .sel(switch__S));  // open: in13, in14, in15
  Multiplexer #(.select(4), .enable("false")) multiplexer_2 (
    .in0(in_5), .in1(in_5), .in2(in_5), .in3(in_5), .in4(in_5), .in5(in_5), .in6(in_5), .in7(in_5),
    .in8(in_5), .in9(in_5), .in10(undriven_4), .in11(undriven_5), .in12(undriven_6), .out(equal),
    .sel(switch__S));  // open: in13, in14, in15
  Demultiplexer #(.select(4), .width(16), .enable("false")) demultiplexer_1 (
    .out0(operation0inX), .out1(operation1inX), .out2(operation2inX), .out3(operation3inX),
    .out4(operation4inX), .out5(operation5inX), .out6(operation6inX), .out7(operation7inX),
    .out8(operation8inX), .out9(operation9inX), .out10(operation10inX), .out11(operation11inX),
    .out12(operation12inX), .in(X), .sel(switch__S));  // open: out13, out14, out15
  Demultiplexer #(.select(4), .width(16), .enable("false")) demultiplexer_2 (
    .out0(operation0inY), .out1(operation1inY), .out2(operation2inY), .out3(operation3inY),
    .out4(operation4inY), .out5(operation5inY), .out6(operation6inY), .out7(operation7inY),
    .out8(operation8inY), .out9(operation9inY), .out10(operation10inY), .out11(operation11inY),
    .out12(operation12inY), .in(Y), .sel(switch__S));  // open: out13, out14, out15
  Negator negator_2 (.in(operation3inY[7:0]), .out(negator_2_out));
  Negator negator_3 (.in(operation3inY[15:8]), .out(negator_3_out));
  Negator negator_4 (.in(operation5inY[7:0]), .out(negator_4_out));
  Negator negator_5 (.in(operation5inX[7:0]), .out(negator_5_out));
  Shifter #(.width(16), .shift("ar")) shifter_1 (.in(operation8inX), .\dist (operation8inY[3:0]), .out(result8));
  _16bitoverflow u_16bitoverflow_1 (
    .Xinput(operation9inX), .Yinput(operation9inY), .overflow(signedOverflow9), .out(result9));
  assign result0 = operation0inX | operation0inY;  // OR_Gate or_1, 16 bits wide
  assign result1 = operation1inX & operation1inY;  // AND_Gate and_1, 16 bits wide
  _8bitoverflow u_8bitoverflow_1 (
    .in_1(operation2inX[7:0]), .in_2(operation2inY[7:0]), .overflow(lowerOverflow2), .out(result2[7:0]));
  _8bitoverflow u_8bitoverflow_2 (
    .in_1(operation2inY[15:8]), .in_2(operation2inX[15:8]), .overflow(upperOverflow2), .out(result2[15:8]));
  _8bitoverflow u_8bitoverflow_3 (
    .in_1(operation3inX[7:0]), .in_2(negator_2_out), .overflow(lowerOverflow3), .out(result3[7:0]));
  _8bitoverflow u_8bitoverflow_4 (
    .in_1(negator_3_out), .in_2(operation3inX[15:8]), .overflow(upperOverflow3), .out(result3[15:8]));
  _8bitoverflow u_8bitoverflow_5 (
    .in_1(operation4inX[7:0]), .in_2(operation4inX[15:8]), .overflow(lowerOverflow4), .out(result4[7:0]));
  _8bitoverflow u_8bitoverflow_6 (
    .in_1(operation4inY[7:0]), .in_2(operation4inY[15:8]), .overflow(upperOverflow4), .out(result4[15:8]));
  _8bitoverflow u_8bitoverflow_7 (
    .in_1(negator_4_out), .in_2(operation5inY[15:8]), .overflow(lowerOverflow5), .out(result5[7:0]));
  _8bitoverflow u_8bitoverflow_8 (
    .in_1(negator_5_out), .in_2(operation5inX[15:8]), .overflow(upperOverflow5), .out(result5[15:8]));
  Shifter #(.width(16)) shifter_2 (.in(operation6inX), .\dist (operation6inY[3:0]), .out(result6));
  Shifter #(.width(16), .shift("lr")) shifter_3 (.in(operation7inX), .\dist (operation7inY[3:0]), .out(result7));
  Multiplexer #(.select(4), .width(16), .enable("false")) multiplexer_3 (
    .in0(result0), .in1(result1), .in2(result2), .in3(result3), .in4(result4), .in5(result5), .in6(result6),
    .in7(result7), .in8(result8), .in9(result9), .in10(result10), .in11(result11), .in12(result12),
    .out(result), .sel(switch__S));  // open: in13, in14, in15
  or or_2 (signedOverflow2, lowerOverflow2, upperOverflow2);
  or or_3 (signedOverflow3, lowerOverflow3, upperOverflow3);
  or or_4 (signedOverflow4, lowerOverflow4, upperOverflow4);
  or or_5 (signedOverflow5, lowerOverflow5, upperOverflow5);
  // Probe on result

  // Other names for the same wires on the sheet: signedOverflow = signed_overflow; switch[3:0] = switch__S;
  //   upperOverflow9 = signedOverflow9

  // Notes on the sheet:
  //   These are INPUTS to your circuit
  //   This is an INPUT to your circuit
  //   addp8:
  //   add:
  //   control of input y
  //   control of signed overflow
  //   control of equal
  //   or:
  //   and:
  //   subp8:
  //   addh8:
  //   subh8:
  //   sllv:
  //   slrv:
  //   slav:
  //   control of input x
  //   DO NOT CHANGE THE LOCATIONS OF THE INPUTS/OUTPUTS! IF YOU DO SO, YOU NEED TO MAKE SURE THE PINS ARE AT THE RIGHT PLACE!
  //   control of output
  //   These are OUTPUTS to your circuit
endmodule

// 8bitAdder
module _8bitoverflow (
  input  [7:0] in_1,
  input  [7:0] in_2,
  output [7:0] out,
  output overflow
);

  wire adder_1_cout, adder_2_cout;

  // Probe on in_2
  // Probe on in_1
  Adder adder_1 (.a(in_2), .b(in_1), .out(out), .cout(adder_1_cout));  // open: cin
  Adder #(.width(7)) adder_2 (.a(in_1[6:0]), .b(in_2[6:0]), .cout(adder_2_cout));  // open: out, cin
  xor xor_1 (overflow, adder_2_cout, adder_1_cout);
  // Probe on out
endmodule

module _16bitoverflow (
  input  [15:0] Xinput,
  input  [15:0] Yinput,
  output [15:0] out,
  output overflow
);

  wire adder_1_cout, adder_2_cout;

  // Probe on Yinput
  // Probe on Xinput
  Adder #(.width(16)) adder_1 (.a(Yinput), .b(Xinput), .out(out), .cout(adder_1_cout));  // open: cin
  Adder #(.width(15)) adder_2 (.a(Xinput[14:0]), .b(Yinput[14:0]), .cout(adder_2_cout));  // open: out, cin
  xor xor_1 (overflow, adder_2_cout, adder_1_cout);
  // Probe on out
endmodule
