// Logisim project cache-harness.circ as structural Verilog: 1 circuit, main circuit Cache-harness
module Cache_harness (
  output [7:0] Test_num,
  output [13:0] Valid_Tag1,
  output [13:0] Valid_Tag3,
  output [15:0] DataOut,
  output [13:0] Valid_Tag0,
  output [13:0] Valid_Tag2,
  output [31:0] Line0,
  output [31:0] Line1,
  output [31:0] Line2,
  output [31:0] Line3
);

  wire clock_1_out;
  wire [7:0] register_1_q;
  wire [15:0] cache_1_p7;
  wire [31:0] cache_1_p5, cache_1_p9, rom_1_data;

  Register register_1 (.D(Test_num), .en(1'b1), .Q(register_1_q), .clk(clock_1_out));  // open: clr
  Adder adder_1 (.a(8'h1), .b(register_1_q), .out(Test_num));  // open: cin, cout
  ROM #(.dataWidth(32)) rom_1 (.addr(register_1_q), .data(rom_1_data), .sel(1'b1));
  Clock clock_1 (.out(clock_1_out));
  // cache cache_1: pin names not known; wires that end beside it: rom_1_data[15:0], rom_1_data[31], clock_1_out, Valid_Tag0, cache_1_p5, Valid_Tag1, cache_1_p7, Valid_Tag2, cache_1_p9, Valid_Tag3, DataOut, Line0, Line1, Line2, Line3
  RAM #(.addrWidth(16), .dataWidth(32), .bus("separate")) ram_1 (
    .addr(cache_1_p7), .din(cache_1_p5), .data(cache_1_p9), .str(1'b1), .sel(1'b1), .clk(clock_1_out),
    .ld(1'b1), .clr(1'b0));

  // Notes on the sheet:
  //   Your Cache should be sitting here!
endmodule
