// Logisim project cache_original.circ as structural Verilog: 1 circuit, main circuit cache
module cache (
  input  [15:0] Address,
  input  [15:0] DataIn,
  input  MemWrite,
  input  Clock,
  input  [31:0] DataFromMemory,
  output [15:0] DataOut,
  output [13:0] Valid_Tag0,
  output [31:0] Line0,
  output [13:0] Valid_Tag1,
  output [31:0] Line1,
  output [13:0] Valid_Tag2,
  output [31:0] Line2,
  output [13:0] Valid_Tag3,
  output [31:0] DataToMemory,
  output [15:0] AddressToMemory,
  output [31:0] Line3
);


  // Notes on the sheet:
  //   These are inputs to your circuit
  //   These are your interface with memory
  //   Do NOT place RAM wthin your own circuit
  //   These are outputs from your circuit
endmodule
