// Logisim project cache_test.circ as structural Verilog: 3 circuits, main circuit cache
module cache (
  input  [15:0] Address,
  input  [15:0] DataIn,
  input  [31:0] DataFromMemory,
  input  Clock,
  input  MemWrite,
  output [15:0] DataOut,
  output [13:0] Valid_Tag0,
  output [31:0] Line0,
  output [13:0] Valid_Tag1,
  output [31:0] Line1,
  output [13:0] Valid_Tag2,
  output [31:0] Line2,
  output [13:0] Valid_Tag3,
  output [31:0] DataToMemory,
  output [15:0] AddressToMemory,
  output [31:0] Line3
);

  copy copy_1 (
    .Address(Address), .DataIn(DataIn), .MemWrite(MemWrite), .Clock(Clock), .DataToMemory(DataToMemory),
    .AddressToMemory(AddressToMemory), .DataFromMemory(DataFromMemory), .DataOut(DataOut),
    .Valid_Tag0(Valid_Tag0), .Line0(Line0), .Valid_Tag1(Valid_Tag1), .Line1(Line1), .Valid_Tag2(Valid_Tag2),
    .Line2(Line2), .Valid_Tag3(Valid_Tag3), .Line3(Line3));

  // Other names for the same wires on the sheet: AddressToMem[15:0] = AddressToMemory; clk = Clock;
  //   DataFromMem[31:0] = DataFromMemory; DataToMem[31:0] = DataToMemory; Detain[15:0] = DataIn; L0[31:0] = Line0;
  //   L1[31:0] = Line1; L2[31:0] = Line2; L3[31:0] = Line3; LS0[13:0] = Valid_Tag0; LS1[13:0] = Valid_Tag1;
  //   LS2[13:0] = Valid_Tag2; LS3[13:0] = Valid_Tag3

  // Notes on the sheet:
  //   These are inputs to your circuit
  //   These are your interface with memory
  //   Do NOT place RAM wthin your own circuit
  //   These are outputs from your circuit
endmodule

// Control
module CacheControl (
  input  hit,
  input  MemWrite,
  output reset,
  output LEnable,
  output FromMem,
  output ReadHit,
  output ReadMiss,
  output WriteMiss,
  output WriteHit
);

  wire not_1_out, not_2_out;

  not not_1 (not_1_out, hit);
  not not_2 (not_2_out, MemWrite);
  and and_1 (ReadMiss, not_2_out, not_1_out);
  and and_2 (WriteMiss, MemWrite, not_1_out);
  and and_3 (ReadHit, not_2_out, hit);
  and and_4 (WriteHit, MemWrite, hit);
  not not_3 (LEnable, ReadHit);
  not not_4 (FromMem, ReadHit);

  assign reset = 1'b0;
endmodule

module copy (
  input  [15:0] Address,
  input  [15:0] DataIn,
  input  MemWrite,
  input  Clock,
  input  [31:0] DataFromMemory,
  output [15:0] DataOut,
  output [13:0] Valid_Tag0,
  output [31:0] Line0,
  output [13:0] Valid_Tag1,
  output [31:0] Line1,
  output [13:0] Valid_Tag2,
  output [31:0] Line2,
  output [13:0] Valid_Tag3,
  output [31:0] DataToMemory,
  output [15:0] AddressToMemory,
  output [31:0] Line3
);

  wire comparator_1_eq, FromMem, hit, L0Enable, L1Enable, L2Enable, L3Enable, LEnable, not_1_out, ReadHit,
       ReadMiss, reset, reset0, reset1, reset2, reset3, undriven, valid, WriteHit, WriteMiss;
  wire [12:0] LStag;
  wire [13:0] LS0Input, LS1Input, LS2Input, LS3Input;
  wire [15:0] multiplexer_1_out, multiplexer_2_out, PrevAddress;
  wire [31:0] controlled_buffer_1_out, L, L0Input, L1Input, L2Input, L3Input, LInput, multiplexer_7_out,
       multiplexer_8_out, multiplexer_12_out, WriteMissOutput;

  Multiplexer #(.width(16), .enable("false")) multiplexer_1 (
    .in0(L[15:0]), .in1(L[31:16]), .out(multiplexer_1_out), .sel(Address[0]));
  Multiplexer #(.width(16), .enable("false")) multiplexer_2 (
    .in0(DataFromMemory[15:0]), .in1(DataFromMemory[31:16]), .out(multiplexer_2_out), .sel(Address[0]));
  Demultiplexer #(.select(2), .enable("false")) demultiplexer_1 (
    .out0(reset0), .out1(reset1), .out2(reset2), .out3(reset3), .in(reset), .sel(Address[2:1]));
  Demultiplexer #(.select(2), .enable("false")) demultiplexer_2 (
    .out0(L0Enable), .out1(L1Enable), .out2(L2Enable), .out3(L3Enable), .in(1'b1), .sel(Address[2:1]));
  Demultiplexer #(.select(2), .width(32), .enable("false")) demultiplexer_3 (
    .out0(L0Input), .out1(L1Input), .out2(L2Input), .out3(L3Input), .in(LInput), .sel(Address[2:1]));
  Demultiplexer #(.select(2), .width(14), .enable("false")) demultiplexer_4 (
    .out0(LS0Input), .out1(LS1Input), .out2(LS2Input), .out3(LS3Input), .in({1'b1, Address[15:3]}),
    .sel(Address[2:1]));
  Register #(.width(16)) register_1 (.D({Address[15:1], 1'b0}), .en(1'b1), .Q(PrevAddress), .clk(Clock));  // open: clr
  Multiplexer #(.width(16), .enable("false")) multiplexer_3 (
    .in0({Address[15:1], 1'b0}), .in1(PrevAddress), .out(AddressToMemory), .sel(ReadHit));
  Multiplexer #(.width(16), .enable("false")) multiplexer_4 (
    .in0(multiplexer_1_out), .in1(multiplexer_2_out), .out(DataOut), .sel(not_1_out));
  not not_1 (not_1_out, hit);
  // Probe on DataOut
  and and_1 (hit, valid, comparator_1_eq);
  Comparator #(.width(13)) comparator_1 (.a(Address[15:3]), .b(LStag), .eq(comparator_1_eq));  // open: gt, lt
  Multiplexer #(.select(2), .enable("false")) multiplexer_5 (
    .in0(Valid_Tag0[13]), .in1(Valid_Tag1[13]), .in2(Valid_Tag2[13]), .in3(Valid_Tag3[13]), .out(valid),
    .sel(Address[2:1]));
  Multiplexer #(.select(2), .width(13), .enable("false")) multiplexer_6 (
    .in0(Valid_Tag0[12:0]), .in1(Valid_Tag1[12:0]), .in2(Valid_Tag2[12:0]), .in3(Valid_Tag3[12:0]),
    .out(LStag), .sel(Address[2:1]));
  // Probe on nothing
  // Probe on LS0Input
  assign controlled_buffer_1_out = WriteHit ? multiplexer_7_out : 32'bz;  // Controlled_Buffer controlled_buffer_1
  Multiplexer #(.width(32), .enable("false")) multiplexer_7 (
    .in0({DataFromMemory[31:16], DataIn}), .in1({DataIn, DataFromMemory[15:0]}), .out(multiplexer_7_out),
    .sel(Address[0]));
  Multiplexer #(.width(32), .enable("false")) multiplexer_8 (
    .in0(controlled_buffer_1_out), .in1(DataFromMemory), .out(multiplexer_8_out), .sel(ReadMiss));
  Multiplexer #(.select(2), .width(32), .enable("false")) multiplexer_9 (
    .in0(Line0), .in1(Line1), .in2(Line2), .in3(Line3), .out(L), .sel(Address[2:1]));
  Register #(.width(14)) LS0 (.D(LS0Input), .en(L0Enable), .Q(Valid_Tag0), .clk(Clock), .clr(reset0));
  Register #(.width(14)) LS1 (.D(LS1Input), .en(L1Enable), .Q(Valid_Tag1), .clk(Clock), .clr(reset1));
  Register #(.width(14)) LS2 (.D(LS2Input), .en(L2Enable), .Q(Valid_Tag2), .clk(Clock), .clr(reset2));
  Register #(.width(14)) LS3 (.D(LS3Input), .en(L3Enable), .Q(Valid_Tag3), .clk(Clock), .clr(reset3));
  Multiplexer #(.width(32), .enable("false")) multiplexer_10 (
    .in0(multiplexer_8_out), .in1(WriteMissOutput), .out(LInput), .sel(WriteMiss));
  // Probe on undriven
  Multiplexer #(.width(32), .enable("false")) multiplexer_11 (
    .in0(LInput), .in1(DataFromMemory), .out(DataToMemory), .sel(ReadHit));
  // Probe on Line0
  Register #(.width(32)) L0 (.D(L0Input), .en(L0Enable), .Q(Line0), .clk(Clock), .clr(reset0));
  // Probe on Line2
  // Probe on Line1
  Register #(.width(32)) L1 (.D(L1Input), .en(L1Enable), .Q(Line1), .clk(Clock), .clr(reset1));
  Register #(.width(32)) L2 (.D(L2Input), .en(L2Enable), .Q(Line2), .clk(Clock), .clr(reset2));
  // Probe on Line3
  Register #(.width(32)) L3 (.D(L3Input), .en(L3Enable), .Q(Line3), .clk(Clock), .clr(reset3));
  CacheControl cachecontrol_1 (
    .hit(hit), .MemWrite(MemWrite), .reset(reset), .LEnable(LEnable), .FromMem(FromMem), .ReadHit(ReadHit),
    .ReadMiss(ReadMiss), .WriteMiss(WriteMiss), .WriteHit(WriteHit));
  Multiplexer #(.width(32), .enable("false")) multiplexer_12 (
    .in0({DataFromMemory[31:16], DataIn}), .in1({DataIn, DataFromMemory[15:0]}), .out(multiplexer_12_out),
    .sel(Address[0]));
  assign WriteMissOutput = WriteMiss ? multiplexer_12_out : 32'bz;  // Controlled_Buffer controlled_buffer_2

  // Other names for the same wires on the sheet: index[1:0] = Address[2:1]; DataFromMem[31:0] = DataFromMemory;
  //   FromMemData1[15:0] = DataFromMemory[31:16]; FromMemData0[15:0] = DataFromMemory[15:0]; Detain[15:0] = DataIn;
  //   offset = Address[0]; AddressToMem[15:0] = AddressToMemory; clk = Clock; DataToMem[31:0] = DataToMemory;
  //   LData0[15:0] = L[15:0]; LData1[15:0] = L[31:16]; L0[31:0] = Line0; L1[31:0] = Line1; L2[31:0] = Line2;
  //   L3[31:0] = Line3; LS0[13:0] = Valid_Tag0; LS0tag[12:0] = Valid_Tag0[12:0]; LS0valid = Valid_Tag0[13];
  //   LS1[13:0] = Valid_Tag1; LS1tag[12:0] = Valid_Tag1[12:0]; LS1valid = Valid_Tag1[13]; LS2[13:0] = Valid_Tag2;
  //   LS2tag[12:0] = Valid_Tag2[12:0]; LS2valid = Valid_Tag2[13]; LS3[13:0] = Valid_Tag3;
  //   LS3tag[12:0] = Valid_Tag3[12:0]; LS3valid = Valid_Tag3[13]; LSInput[12:0] = Address[15:3];
  //   tag[12:0] = Address[15:3]

  // Notes on the sheet:
  //   Break down of address
  //   These are inputs to your circuit
  //   All below are just feed in
  //   Save the older address
  //   fetch the data only if not hit
  //   Data to circuit is determined here
  //   Hit or not?
  //   line0
  //   line1
  //   line2
  //   line3
  //   line2
  //   Which line has what?
  //   These are your interface with memory
  //   Do NOT place RAM wthin your own circuit
  //   what comes into the below line
  //   Input
  //   what goes to mem
  //   control is here
  //   Special for WriteMiss
  //   These are outputs from your circuit
endmodule
