// Logisim project cpu.circ as structural Verilog: 3 circuits, main circuit main
module main (
  input  [15:0] From_Instr_Mem,
  input  clk,
  output [15:0] r0,
  output [15:0] r1,
  output [15:0] r2,
  output [15:0] r3,
  output [15:0] Display_0,
  output [15:0] Display_1,
  output [15:0] To_Instr_Mem,
  output [15:0] Data_Mem_Data,
  output [15:0] Data_Mem_Addr,
  output Data_Mem_Write
);

  wire adder_1_cout, ALUscr, and_1_out, branch, branchne, branchornot, demultiplexer_1_out0,
       demultiplexer_1_out1, Display, J, Jal, Jr, lui, main_2_equal, main_2_signed_overflow, MemRead,
       not_1_out, not_2_out, or_1_out, or_2_out, RegDst, RegWrite, SetReg, undriven, zerosign;
  wire [1:0] multiplexer_1_out, multiplexer_3_out;
  wire [3:0] ALUcontrol;
  wire [15:0] adder_2_out, afterpipe, bit_extender_1_out, bit_extender_2_out, DataDisp, DataWrite,
       DataWriteNormI, extended, jraddress, memory_1_output, multiplexer_2_out, multiplexer_4_out,
       multiplexer_5_out, multiplexer_8_out, multiplexer_9_out, multiplexer_10_out, shifter_1_out, ToPC_1;

  ROM #(.addrWidth(16), .dataWidth(16)) rom_1 ();  // open: addr, data, sel
  // Probe on undriven
  Multiplexer #(.width(2), .enable("false")) multiplexer_1 (
    .in0(afterpipe[9:8]), .in1(afterpipe[7:6]), .out(multiplexer_1_out), .sel(RegDst));
  Multiplexer #(.width(16), .enable("false")) multiplexer_2 (
    .in0(From_Instr_Mem), .in1({16{1'b0}}), .out(multiplexer_2_out), .sel(or_1_out));
  or or_1 (or_1_out, branchornot, Jr, Jal, J);
  Multiplexer #(.width(2), .enable("false")) multiplexer_3 (
    .in0(multiplexer_1_out), .in1(2'b11), .out(multiplexer_3_out), .sel(Jal));
  Register #(.width(16)) register_1 (.D(multiplexer_2_out), .en(1'b1), .Q(afterpipe), .clk(clk));  // open: clr
  Multiplexer #(.width(16), .enable("false")) multiplexer_4 (
    .in0(DataWrite), .in1(To_Instr_Mem), .out(multiplexer_4_out), .sel(Jal));
  Regfile_main main_1 (
    .Read_register_1(afterpipe[11:10]), .Read_register_2(afterpipe[9:8]), .write_register(multiplexer_3_out),
    .write_data(multiplexer_4_out), .Reg_0_Value(r0), .Reg_1_Value(r1), .Reg_2_Value(r2), .Reg_3_Value(r3),
    .RegWrite(RegWrite), .SetReg(SetReg), .clock(clk), .Read_Data_1(DataDisp), .Read_Data_2(Data_Mem_Data));
  alu_main main_2 (
    .switch__S(ALUcontrol), .X(DataDisp), .equal(main_2_equal), .result(Data_Mem_Addr),
    .signed_overflow(main_2_signed_overflow), .Y(multiplexer_5_out));
  and and_1 (and_1_out, branch, main_2_equal);
  LED led_1 (.in(main_2_signed_overflow));
  Multiplexer #(.width(16), .enable("false")) multiplexer_5 (
    .in0(Data_Mem_Data), .in1(extended), .out(multiplexer_5_out), .sel(ALUscr));
  Hex_Digit_Display hex_digit_display_1 (.value(Display_0[11:8]));  // open: dp
  Hex_Digit_Display hex_digit_display_2 (.value(Display_0[15:12]));  // open: dp
  not not_1 (not_1_out, and_1_out);
  assign jraddress = Jr ? DataDisp : 16'bz;  // Controlled_Buffer controlled_buffer_1
  Hex_Digit_Display hex_digit_display_3 (.value(Display_0[7:4]));  // open: dp
  Hex_Digit_Display hex_digit_display_4 (.value(Display_0[3:0]));  // open: dp
  Multiplexer #(.enable("false")) multiplexer_6 (.in0(and_1_out), .in1(not_1_out), .out(branchornot), .sel(branchne));
  Hex_Digit_Display hex_digit_display_5 (.value(Display_1[15:12]));  // open: dp
  // Probe on nothing
  Register #(.width(16)) register_2 (.D(DataDisp), .en(demultiplexer_1_out0), .Q(Display_0), .clk(clk));  // open: clr
  Demultiplexer #(.enable("false")) demultiplexer_1 (
    .out0(demultiplexer_1_out0), .out1(demultiplexer_1_out1), .in(Display), .sel(afterpipe[0]));
  Hex_Digit_Display hex_digit_display_6 (.value(Display_1[7:4]));  // open: dp
  Hex_Digit_Display hex_digit_display_7 (.value(Display_1[11:8]));  // open: dp
  memory memory_1 (
    .Detain(Data_Mem_Data), .Address(Data_Mem_Addr), .clk(clk), .\output (memory_1_output),
    .MemWrite(Data_Mem_Write));
  Hex_Digit_Display hex_digit_display_8 (.value(Display_1[3:0]));  // open: dp
  not not_2 (not_2_out, MemRead);
  Register #(.width(16)) register_3 (.D(DataDisp), .en(demultiplexer_1_out1), .Q(Display_1), .clk(clk));  // open: clr
  Multiplexer #(.width(16), .enable("false")) multiplexer_7 (
    .in0(memory_1_output), .in1(Data_Mem_Addr), .out(DataWriteNormI), .sel(not_2_out));
  // Probe on To_Instr_Mem
  Adder #(.width(16)) adder_1 (.a(To_Instr_Mem), .b(16'h1), .out(ToPC_1), .cout(adder_1_cout));  // open: cin
  LED led_2 (.in(adder_1_cout));
  Multiplexer #(.width(16), .enable("false")) multiplexer_8 (
    .in0(ToPC_1), .in1(adder_2_out), .out(multiplexer_8_out), .sel(branchornot));
  Adder #(.width(16)) adder_2 (.a(To_Instr_Mem), .b(extended), .out(adder_2_out));  // open: cin, cout
  assign bit_extender_1_out = {{8{afterpipe[7]}}, afterpipe[7:0]};  // Bit_Extender bit_extender_1
  assign bit_extender_2_out = {{8{1'b0}}, afterpipe[7:0]};  // Bit_Extender bit_extender_2
  Multiplexer #(.width(16), .enable("false")) multiplexer_9 (
    .in0(multiplexer_10_out), .in1({To_Instr_Mem[15:12], afterpipe[11:0]}), .out(multiplexer_9_out),
    .sel(or_2_out));
  Multiplexer #(.width(16), .enable("false")) multiplexer_10 (
    .in0(multiplexer_8_out), .in1(jraddress), .out(multiplexer_10_out), .sel(Jr));
  or or_2 (or_2_out, Jal, J);
  Multiplexer #(.width(16), .enable("false")) multiplexer_11 (
    .in0(bit_extender_1_out), .in1(bit_extender_2_out), .out(extended), .sel(zerosign));
  // Probe on multiplexer_9_out
  Register #(.width(16)) register_4 (.D(multiplexer_9_out), .en(1'b1), .Q(To_Instr_Mem), .clk(clk));  // open: clr
  control control_1 (
    .opcode(afterpipe[15:12]), .rs(afterpipe[11:10]), .rt(afterpipe[9:8]), .rd(afterpipe[7:6]),
    .func(afterpipe[5:0]), .jaddress(afterpipe[11:0]), .imm(afterpipe[7:0]), .ALUcontrol(ALUcontrol),
    .ALUscr(ALUscr), .branch(branch), .branchne(branchne), .RegWrite(RegWrite), .SetReg(SetReg),
    .Display(Display), .MemRead(MemRead), .zerosign(zerosign), .MemWrite(Data_Mem_Write), .J(J), .Jal(Jal),
    .Jr(Jr), .RegDst(RegDst), .lui(lui));
  Shifter #(.width(16)) shifter_1 (.in(extended), .\dist (4'b1000), .out(shifter_1_out));
  // Probe on ALUcontrol
  Multiplexer #(.width(16), .enable("false")) multiplexer_12 (
    .in0(DataWriteNormI), .in1(shifter_1_out), .out(DataWrite), .sel(lui));
  // Probe on nothing

  // Other names for the same wires on the sheet: opcode[3:0] = afterpipe[15:12]; ALUOutput[15:0] = Data_Mem_Addr;
  //   d0[15:0] = Display_0; d1[15:0] = Display_1; DatainMem[15:0] = Data_Mem_Data; func[5:0] = afterpipe[5:0];
  //   imm[7:0] = afterpipe[7:0]; Jaddress[11:0] = afterpipe[11:0];
  //   JaddressStore[15:0] = {To_Instr_Mem[15:12], afterpipe[11:0]}; rd[1:0] = afterpipe[7:6];
  //   rt[1:0] = afterpipe[9:8]; rs[1:0] = afterpipe[11:10]; ToPC[15:0] = To_Instr_Mem; MemWrite = Data_Mem_Write

  // Notes on the sheet:
  //   instruction decompose
  //   contents of rom_1 (hex, n*v repeats v):
  //   b035 8123 802d 489
  //   This is the current PC that you need to send as OUTPUT
  //   This is the instruction that you would receive as INPUT
  //   ALU_Register
  //   This is a CLK that is an INPUT driven from the harness.
  //   Remember, this circuit is loaded from the harness to be tested!
  //   These are OUTPUTS to the circuit
  //   DO NOT CHANGE THE LOCATIONS OF THE INPUTS/OUTPUTS! IF YOU DO SO, YOU NEED TO MAKE SURE THE PINS ARE AT THE RIGHT PLACE!
  //   The memory
  //   The displays
  //   These are OUTPUTS to the circuit
  //   pipeline
  //   sign extension
  //   lui special routing
endmodule

// Memory
module memory (
  input  [15:0] Detain,
  input  [15:0] Address,
  input  clk,
  input  MemWrite,
  output [15:0] \output 
);

  wire not_1_out;

  assign \output  = MemWrite ? Detain : 16'bz;  // Controlled_Buffer controlled_buffer_1
  RAM #(.addrWidth(16), .dataWidth(16)) ram_1 (
    .addr(Address), .data(\output ), .sel(1'b1), .clk(clk), .ld(not_1_out));  // open: clr
  not not_1 (not_1_out, MemWrite);
endmodule

module control (
  input  [3:0] opcode,
  input  [1:0] rs,
  input  [1:0] rt,
  input  [1:0] rd,
  input  [5:0] func,
  input  [11:0] jaddress,
  input  [7:0] imm,
  output [3:0] ALUcontrol,
  output ALUscr,
  output branch,
  output branchne,
  output RegWrite,
  output SetReg,
  output Display,
  output MemRead,
  output zerosign,
  output MemWrite,
  output J,
  output Jal,
  output Jr,
  output RegDst,
  output lui
);

  wire and_16_out, and_17_out, and_18_out, and_19_out, and_20_out, and_21_out, and_22_out, and_23_out,
       and_24_out, and_25_out, and_26_out, and_27_out, C2, C6, C7, C8, C14, not_1_out, not_2_out, not_3_out,
       not_4_out, not_5_out, not_6_out, not_7_out, not_8_out, not_9_out, or_1_out, R0, R1, R2, R3, R4, R5,
       R6, R7, R8, R9, R10, R11;

  not not_1 (not_1_out, opcode[3]);
  not not_2 (not_2_out, opcode[1]);
  not not_3 (not_3_out, opcode[2]);
  not not_4 (not_4_out, opcode[0]);
  and and_1 (RegDst, not_1_out, not_3_out, not_2_out, not_4_out);
  and and_2 (branchne, not_1_out, not_3_out, not_2_out, opcode[0]);
  and and_3 (C2, not_1_out, not_3_out, opcode[1], not_4_out);
  and and_4 (J, not_1_out, not_3_out, opcode[1], opcode[0]);
  and and_5 (Jr, not_1_out, opcode[2], not_2_out, not_4_out);
  and and_6 (Jal, not_1_out, opcode[2], not_2_out, opcode[0]);
  and and_7 (C6, not_1_out, opcode[2], opcode[1], not_4_out);
  and and_8 (C7, not_1_out, opcode[2], opcode[1], opcode[0]);
  and and_9 (C8, opcode[3], not_3_out, not_2_out, not_4_out);
  and and_10 (MemWrite, opcode[3], not_3_out, not_2_out, opcode[0]);
  and and_11 (MemRead, opcode[3], not_3_out, opcode[1], not_4_out);
  and and_12 (lui, opcode[3], not_3_out, opcode[1], opcode[0]);
  and and_13 (Display, opcode[3], opcode[2], not_2_out, not_4_out);
  and and_14 (SetReg, opcode[3], opcode[2], not_2_out, opcode[0]);
  and and_15 (C14, opcode[3], opcode[2], opcode[1], not_4_out);
  not not_5 (not_5_out, func[3]);
  not not_6 (not_6_out, func[1]);
  not not_7 (not_7_out, func[2]);
  not not_8 (not_8_out, func[0]);
  and and_16 (and_16_out, not_5_out, not_7_out, not_6_out, not_8_out);
  and and_17 (and_17_out, not_5_out, not_7_out, not_6_out, func[0]);
  and and_18 (and_18_out, not_5_out, not_7_out, func[1], not_8_out);
  and and_19 (and_19_out, not_5_out, not_7_out, func[1], func[0]);
  and and_20 (and_20_out, not_5_out, func[2], not_6_out, not_8_out);
  and and_21 (and_21_out, not_5_out, func[2], not_6_out, func[0]);
  and and_22 (and_22_out, not_5_out, func[2], func[1], not_8_out);
  and and_23 (and_23_out, not_5_out, func[2], func[1], func[0]);
  and and_24 (and_24_out, func[3], not_7_out, not_6_out, not_8_out);
  and and_25 (and_25_out, func[3], not_7_out, not_6_out, func[0]);
  and and_26 (and_26_out, func[3], not_7_out, func[1], not_8_out);
  and and_27 (and_27_out, func[3], not_7_out, func[1], func[0]);
  and and_28 (R0, and_16_out, RegDst);
  and and_29 (R1, and_17_out, RegDst);
  and and_30 (R2, and_18_out, RegDst);
  and and_31 (R3, and_19_out, RegDst);
  and and_32 (R4, and_20_out, RegDst);
  and and_33 (R5, and_21_out, RegDst);
  and and_34 (R6, and_22_out, RegDst);
  and and_35 (R7, and_23_out, RegDst);
  and and_36 (R8, and_24_out, RegDst);
  and and_37 (R9, and_25_out, RegDst);
  and and_38 (R10, and_26_out, RegDst);
  and and_39 (R11, and_27_out, RegDst);
  assign ALUcontrol = R0 ? 4'b0000 : 4'bz;  // Controlled_Buffer controlled_buffer_1
  assign ALUcontrol = R1 ? 4'b0001 : 4'bz;  // Controlled_Buffer controlled_buffer_2
  assign ALUcontrol = R2 ? 4'b0010 : 4'bz;  // Controlled_Buffer controlled_buffer_3
  assign ALUcontrol = R3 ? 4'b0011 : 4'bz;  // Controlled_Buffer controlled_buffer_4
  assign ALUcontrol = R4 ? 4'b0100 : 4'bz;  // Controlled_Buffer controlled_buffer_5
  assign ALUcontrol = R5 ? 4'b0101 : 4'bz;  // Controlled_Buffer controlled_buffer_6
  assign ALUcontrol = R6 ? 4'b0110 : 4'bz;  // Controlled_Buffer controlled_buffer_7
  assign ALUcontrol = R7 ? 4'b0111 : 4'bz;  // Controlled_Buffer controlled_buffer_8
  assign ALUcontrol = R8 ? 4'b1000 : 4'bz;  // Controlled_Buffer controlled_buffer_9
  assign ALUcontrol = R9 ? 4'b1001 : 4'bz;  // Controlled_Buffer controlled_buffer_10
  assign ALUcontrol = R10 ? 4'b1010 : 4'bz;  // Controlled_Buffer controlled_buffer_11
  assign ALUcontrol = R11 ? 4'b1011 : 4'bz;  // Controlled_Buffer controlled_buffer_12
  assign ALUcontrol = C14 ? 4'b1100 : 4'bz;  // Controlled_Buffer controlled_buffer_13
  or or_1 (or_1_out, C6, RegDst, C7, C8, MemWrite, C14, MemRead);
  not not_9 (not_9_out, or_1_out);
  assign ALUcontrol = C6 ? 4'b1001 : 4'bz;  // Controlled_Buffer controlled_buffer_14
  assign ALUcontrol = C7 ? 4'b0001 : 4'bz;  // Controlled_Buffer controlled_buffer_15
  assign ALUcontrol = C8 ? 4'b0000 : 4'bz;  // Controlled_Buffer controlled_buffer_16
  assign ALUcontrol = MemWrite ? 4'b1001 : 4'bz;  // Controlled_Buffer controlled_buffer_17
  assign ALUcontrol = MemRead ? 4'b1001 : 4'bz;  // Controlled_Buffer controlled_buffer_18
  Multiplexer #(.width(4), .enable("false")) multiplexer_1 (
    .in1(4'b1111), .out(ALUcontrol), .sel(not_9_out));  // open: in0
  or or_2 (branch, branchne, C2);
  or or_3 (zerosign, C7, C8, lui, Display, C14);
  or or_4 (ALUscr, C6, C7, C8, MemWrite, MemRead, lui, Display, SetReg, C14);
  or or_5 (RegWrite, R0, R1, R2, R3, R4, R5, R6, R7, R8, R9, R10, R11, Jal, C6, C7, C8, MemRead, lui, C14);

  // Other names for the same wires on the sheet: C1 = branchne; C3 = J; C4 = Jr; C5 = Jal; C9 = MemWrite;
  //   C10 = MemRead; C11 = lui; C12 = Display; C13 = SetReg; CR = RegDst

  // Notes on the sheet:
  //   input
  //   output
endmodule
